# Fritzing sketch Proyecto_05-Alarm_System (saved by Fritzing 0.9.2b)
breadboards: 1

parts:
  Componente1 = Arduino Uno (Rev3)
  J1 = Piezo Speaker
  S1 = Tilt Switch [package=THT]
  LED1 = LED - 5mm [color="Red (633nm)" package="5 mm [THT]"]
  KEYPAD1 = Membrane Matrix Keypad
  S2 = SWITCH-MOMENTARY-2 [package=tactile_switch_tall]  # not connected
  R1 = Resistor [tolerance=±5% resistance=10k package=THT]
  R2 = Photocell (LDR) [package=THT]
  R3 = Resistor [tolerance=±5% resistance=220 package=THT]

nets (from the breadboard view):
  N1: Componente1.A0, R1.Pin_0, R2.pin_1
  N2: Componente1.D8, KEYPAD1.7
  N3: Componente1.D9_PWM, KEYPAD1.6
  N4: Componente1.D10_PWM/SS, KEYPAD1.5
  N5: Componente1.D11_PWM/MOSI, KEYPAD1.4
  N6: Componente1.D12/MISO, KEYPAD1.3
  N7: Componente1.GND, J1.pin1, S1.Pin_1, LED1.cathode, R1.Pin_1
  N8: Componente1.D2, S1.Pin_2
  N9: Componente1.D3_PWM, R3.Pin_1
  N10: Componente1.D5_PWM, J1.pin2
  N11: Componente1.D6_PWM, KEYPAD1.1
  N12: Componente1.D7, KEYPAD1.2
  N13: Componente1.5V, R2.pin_0
  N14: LED1.anode, R3.Pin_0

custom parts:
  Membrane Matrix Keypad: Membrane Matrix 3x4 Keypad
